// Logisim project 25520585_LuongQuocHoang_IT012.R11.2_TN1.circ as structural Verilog: 1 circuit, main circuit main
module main (
  input  A,
  input  B,
  input  C,
  output XA,
  output AND_A_B,
  output NAND_A_B_C,
  output OR_A_B,
  output XOR_A_B_C,
  output NAND_A_B,
  output NOR_A_B,
  output CHAIN,
  output XOR_A_B,
  output XNOR_A_B
);

  wire nand_2_out;

  not not_1 (XA, A);
  and and_1 (AND_A_B, A, B);
  or or_1 (OR_A_B, A, B);
  nand nand_1 (NAND_A_B, A, B);
  nor nor_1 (NOR_A_B, A, B);
  xor xor_1 (XOR_A_B, A, B);
  xnor xnor_1 (XNOR_A_B, A, B);
  nand nand_2 (nand_2_out, A, B);
  nand nand_3 (NAND_A_B_C, A, B, C);
  NotExactlyOne xnor_2 (.out(XOR_A_B_C), .in0(A), .in1(B), .in2(C));
  nand nand_4 (CHAIN, nand_2_out, C);
endmodule
