// Logisim project 25520585_LuongQuocHoang_IT012.R11.2_TN2.circ as structural Verilog: 1 circuit, main circuit main
module main (
  input  x,
  input  y,
  input  z,
  output x_y__prime,
  output EQ1,
  output x_prime_y_prime,
  output EQ2,
  output xy__prime,
  output x_yz,
  output EQ3,
  output x___y__x___z,
  output x___x_prime_y,
  output EQ4,
  output x_y,
  output EQ5
);

  wire EQ2_2_out, EQ2_3_out, EQ2_out, EQ3_out, not_1_out, not_2_out;

  not not_1 (not_1_out, x);
  not not_2 (not_2_out, y);
  nand u_EQ1 (x_y__prime, x, y);
  or EQ1_2 (x_prime_y_prime, not_1_out, not_2_out);
  nor EQ1_3 (xy__prime, x, y);
  and u_EQ2 (EQ2_out, y, z);
  or EQ2_2 (EQ2_2_out, x, y);
  or EQ2_3 (EQ2_3_out, x, z);
  and u_EQ3 (EQ3_out, not_1_out, y);
  or u_EQ5 (x_y, x, y);
  or EQ2_4 (x_yz, EQ2_out, x);
  and EQ2_5 (x___y__x___z, EQ2_2_out, EQ2_3_out);
  or EQ3_2 (x___x_prime_y, EQ3_out, x);
  xnor xnor_1 (EQ1, x_y__prime, x_prime_y_prime);
  xnor xnor_2 (EQ2, x_prime_y_prime, xy__prime);
  xnor xnor_3 (EQ3, x_yz, x___y__x___z);
  xnor xnor_4 (EQ4, x___x_prime_y, x);
  xnor xnor_5 (EQ5, x___x_prime_y, x_y);
endmodule
