// Logisim project 25520585_LuongQuocHoang_IT012.R11.2_TN4.circ as structural Verilog: 1 circuit, main circuit main
module main (
  input  A,
  input  B,
  input  C,
  input  D,
  output F_can,
  output EQ1,
  output F_sop,
  output EQ2,
  output F_pos
);

  wire and_1_out, and_2_out, and_3_out, and_4_out, and_5_out, and_6_out, and_7_out, and_8_out, and_9_out,
       and_10_out, and_11_out, not_1_out, not_2_out, not_3_out, not_4_out, or_1_out, or_2_out, or_3_out,
       or_4_out, or_5_out;

  not not_1 (not_1_out, A);
  not not_2 (not_2_out, B);
  not not_3 (not_3_out, C);
  not not_4 (not_4_out, D);
  and and_1 (and_1_out, not_1_out, not_2_out, C);
  and and_2 (and_2_out, not_1_out, C, D);
  and and_3 (and_3_out, not_1_out, C, D);
  and and_4 (and_4_out, C, not_3_out, D);
  and and_5 (and_5_out, A, not_2_out, C, D);
  or or_1 (or_1_out, B, C);
  or or_2 (or_2_out, C, D);
  or or_3 (or_3_out, not_2_out, not_3_out);
  or or_4 (or_4_out, not_1_out, C);
  or or_5 (or_5_out, not_1_out, not_2_out, not_3_out);
  and and_6 (and_6_out, not_1_out, not_2_out, C, not_4_out);
  and and_7 (and_7_out, not_1_out, not_2_out, C, D);
  and and_8 (and_8_out, not_1_out, B, not_3_out, D);
  and and_9 (and_9_out, not_1_out, B, C, D);
  and and_10 (and_10_out, A, not_2_out, C, D);
  and and_11 (and_11_out, A, B, not_3_out, D);
  or or_6 (F_can, and_6_out, and_7_out, and_8_out, and_9_out, and_10_out, and_11_out);
  or or_7 (F_sop, and_1_out, and_2_out, and_3_out, and_4_out, and_5_out);
  and and_12 (F_pos, or_1_out, or_2_out, or_3_out, or_4_out, or_5_out);
  xnor xnor_1 (EQ1, F_can, F_sop);
  xnor xnor_2 (EQ2, F_can, F_pos);
endmodule
